# Fritzing sketch RXS STATOR (saved by Fritzing 0.9.3b)
breadboards: 1

parts:
  CDI_PULSE = Inductor [package="0805 [SMD]"]
  4_PIN_CONNECTOR = Molex Picoblade Series Header [part_number="(TO LOOM)" package=Picoblade-53261-0419]
  LOOSE_CONNECTORS = Molex Picoblade Series Header [part_number="(TO CDI)" package=Picoblade-53261-0219]
  CDI_POWER = Inductor [package="0805 [SMD]"]
  COIL_2 = Inductor [package="0805 [SMD]"]
  NEUTRAL_SWITCH = SWITCH-MOMENTARY-2 [package=tactile-pth]
  COIL_1 = Inductor [package="0805 [SMD]"]

nets:
  GND: CDI_PULSE.pin_0, 4_PIN_CONNECTOR.4, CDI_POWER.pin_0, NEUTRAL_SWITCH.1, COIL_1.pin_1
  N1: CDI_PULSE.pin_1, LOOSE_CONNECTORS.1
  N2: 4_PIN_CONNECTOR.1, NEUTRAL_SWITCH.2
  N3: 4_PIN_CONNECTOR.2, COIL_2.pin_0
  N4: 4_PIN_CONNECTOR.3, COIL_2.pin_1, COIL_1.pin_0
  N5: LOOSE_CONNECTORS.2, CDI_POWER.pin_1

notes:
  SB
  W/R
  Y
  G/R
  B
  B/R
  GROUND (VIA BODY)
  RXS100 STATOR ASSEMBLY
  DRAWN BY ANTONY CARTWRIGHT - antony@accbs.co.uk
